# Fritzing sketch sketch (saved by Fritzing 0.9.2b)
breadboards: 1

parts:
  Part1 = Intel Edison Arduinobreakout
  Q1 = LTR-301 [package=ltr-301]  # not connected
  U1 = LIPO-2000mAh [package=lipo-2000]
  J1 = Infrared Proximity Sensor  # not connected
  CHARGER1 = USB_LiIon_LiPoly_Charger_v1.2
  Solar_pannel1 = solar_pannel
  IC1 = Switching step-up voltage regulator [package=sot23-5]

nets:
  N1: Part1.GND, IC1.NC
  N2: Part1.VIN, IC1.OUT
  N3: U1.+, CHARGER1.batt_plus_1
  N4: U1.-, CHARGER1.batt_minus_1
  N5: CHARGER1.dcin_minus_1, Solar_pannel1.aún_sin_nombre#0
  N6: CHARGER1.dcin_plus_1, Solar_pannel1.aún_sin_nombre#1
  N7: CHARGER1.load_minus_1, IC1.GND
  N8: CHARGER1.load_plus_1, IC1.LX

custom parts:
  solar_pannel: Solar pannel
